# Fritzing sketch Liquid Pump Schematic (saved by Fritzing 0.9.3b)
circuit board: 6.88566cm x 5.36311cm
breadboards: 1

parts:
  Buzzer = Piezo Speaker
  Water_Level_Sensor = Soil Moisture Sensor
  IC1 = L293D [package=THT]
  Arduino_101 = Genuino 101
  Enable_Status_LED = LED - 3mm [color="Green (570nm)" package="3 mm [THT]"]
  Error_Status_LED = LED - 3mm [color="Red (633nm)" package="3 mm [THT]"]
  R1 = Resistor [tolerance=±5% resistance=470 package="0805 [SMD]"]
  R2 = Resistor [tolerance=±5% resistance=470 package="0805 [SMD]"]
  J1_to_pump = Screw terminal - 2 pins [package=THT]
  R3 = Resistor [tolerance=±5% resistance=10k package="0805 [SMD]"]
  R4 = Resistor [tolerance=±5% resistance=10k package="0805 [SMD]"]

nets:
  GND: Buzzer.pin1, Water_Level_Sensor.GND, IC1.0V, Arduino_101.GND, Enable_Status_LED.cathode, Error_Status_LED.cathode, R3.Pin_1, R4.Pin_0
  N1: Buzzer.pin2, Arduino_101.D2
  N2: Water_Level_Sensor.SIG, Arduino_101.A0
  VCC: Water_Level_Sensor.VCC, Arduino_101.3V3, R2.Pin_0
  N3: IC1.Enable_1, Arduino_101.D3_PWM, R4.Pin_1
  N4: IC1.In_1, Arduino_101.D4
  N5: IC1.Out_1_(_Controlled_by_Enable_1_), J1_to_pump.pin1
  N6: IC1.Out_2_(_Controlled_by_Enable_1_), J1_to_pump.pin2
  N7: IC1.In_2, Arduino_101.D8
  N8: IC1.+Vmotor, Arduino_101.VIN
  N9: IC1.Enable_2, R3.Pin_0
  N10: IC1.+V, Arduino_101.5V
  N11: Arduino_101.D13/SCK, R1.Pin_0
  N12: Enable_Status_LED.anode, R2.Pin_1
  N13: Error_Status_LED.anode, R1.Pin_1

notes:
  Representing Water Level Sensor

custom parts:
  Genuino 101: A learning and development board that delivers the performance and low-power consumption of the Intel® Curie™ Module with the simplicity of Arduino at an entry-level price. It keeps the same robust form factor and peripheral list of the UNO with the addition of onboard Bluetooth LE capabilities and a 6-axis accelerometer/gyro to help you easily expand your creativity into the connected world.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

// code stored in the sketch: Water Refil Schematic.ino

